// Digital circuit rjstack.dig as structural Verilog
module rjstack (
  input  clk,
  input  store,
  input  [15:0] instr,
  output [15:0] ros,
  output [15:0] tos,
  output [11:0] sp,
  output [15:0] nos,
  output [15:0] y,
  output [7:0] i
);

  wire [2:0] pc_out;
  wire [7:0] microcode_d, program_d;
  wire [15:0] bitextender_1_out;

  Counter #(.Bits(3)) pc (.en(1'b1), .C(clk), .clr(1'b0), .out(pc_out));  // open: ovf
  EEPROMDualPort #(.AddrBits(3), .Bits(16)) \program  (
    .A(pc_out), .Din(instr), .str(store), .C(clk), .ld(1'b1), .D({i, program_d}));
  ROM #(.AddrBits(8), .Bits(8)) microcode (.A(program_d), .sel(1'b1), .D(microcode_d));
  LED push (.in(microcode_d[0]));
  LED pop (.in(microcode_d[1]));
  LED i__gt_tos (.in(microcode_d[2]));
  LED nos__gt_tos (.in(microcode_d[3]));
  LED y__gt_tos (.in(microcode_d[4]));
  BitExtender bitextender_1 (.in(i), .out(bitextender_1_out));
  stack stack_1 (
    .clk(clk), .push(microcode_d[0]), .pop(microcode_d[1]), .we_itos(microcode_d[2]),
    .we_nostos(microcode_d[3]), .we_ytos(microcode_d[4]), .i(bitextender_1_out), .y(y), .sp(sp), .ros(ros),
    .nos(nos), .tos(tos));
  Add #(.Bits(16)) alu (.a(nos), .b(tos), .c_i(1'b0), .s(y));  // open: c_o

  // Other names for the same wires on the sheet: c = clk

  // Notes on the sheet:
  //   [02]
  //   rj45Creates
  //   FPGA Stack Machine CPU from Scratch
  //   contents of program (hex, n*v repeats v):
  //   101,201,2,401,2
  //   Microcode and Assembler
  //   contents of microcode (hex, n*v repeats v):
  //   0,5,12,a,9
endmodule
